# Fritzing sketch schematic (saved by Fritzing 0.9.4)
breadboards: 1

parts:
  Raspberry_Pi_1 = Raspberry Pi 3 [part_number=RPI-3-V1.2]
  Display1 = LCD screen 16x2 IIC [part_number=101290]
  J1 = Basic Servo
  J2 = Basic Servo

nets:
  N1: Raspberry_Pi_1.GPIO2, Display1.SDA
  N2: Raspberry_Pi_1.GPIO3, Display1.SCL
  N3: Raspberry_Pi_1.GIPO13, J2.pulse
  GND: Raspberry_Pi_1.GND, Display1.GND
  N4: Raspberry_Pi_1.GIPO12, J1.pulse
  VCC: Raspberry_Pi_1.5V, Display1.VCC, J1.vcc
  GND_2: J1.gnd, J2.gnd

custom parts:
  LCD screen 16x2 IIC: LCD screen with HD44780 controller enables showing text, symbols, value or anything else that comes from Croduino/Arduino. It is capable of showing 16 symbols in two lines and therefore can be used in many projects that need to send clearly visible and legible output information.. • Color of symbols: White • Backlight: Blue • Dimensions: 80 x 36 x 12 mm • Screen dimensions: 64.5 x 16 mm •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
